# Fritzing sketch 02 Button LED (saved by Fritzing 0.9.3b)
breadboards: 1

parts:
  LED1 = LED - 5mm [color="Red (633nm)" package="5 mm [THT]"]
  Part1 = Arduino Uno (Rev3) - ICSP
  R1 = Resistor [tolerance=±5% resistance=220 package=THT]
  S1 = Pushbutton [package="[THT]"]
  R2 = Resistor [tolerance=±5% resistance=10k package=THT]

nets:
  N1: LED1.cathode, R1.Pin_0
  N2: LED1.anode, Part1.D9_PWM
  N3: Part1.D11_PWM/MOSI, S1.Pin_3, S1.Pin_4, R2.Pin_0
  N4: Part1.5V, S1.Pin_1, S1.Pin_2
  N5: Part1.GND, R1.Pin_1, R2.Pin_1
