# Fritzing sketch 08 Int Flowing LEDs (saved by Fritzing 0.9.2b)
breadboards: 1

parts:
  LED1 = LED - 5mm [color="Red (633nm)" package="5 mm [THT]"]
  Part1 = Arduino Uno (Rev3) - ICSP
  R1 = Resistor [tolerance=±5% resistance=220 package=THT]
  LED2 = LED - 5mm [color="Yellow (585nm)" package="5 mm [THT]"]
  LED3 = LED - 5mm [color="Green (560nm)" package="5 mm [THT]"]
  LED4 = LED - 5mm [color="White (6500K)" package="5 mm [THT]"]
  LED5 = LED - 5mm [color="Red (633nm)" package="5 mm [THT]"]
  LED6 = LED - 5mm [color="Yellow (585nm)" package="5 mm [THT]"]
  LED7 = LED - 5mm [color="Green (560nm)" package="5 mm [THT]"]
  LED8 = LED - 5mm [color="White (6500K)" package="5 mm [THT]"]
  R2 = Resistor [tolerance=±5% resistance=220 package=THT]
  R3 = Resistor [tolerance=±5% resistance=220 package=THT]
  R4 = Resistor [tolerance=±5% resistance=220 package=THT]
  R5 = Resistor [tolerance=±5% resistance=220 package=THT]
  R6 = Resistor [tolerance=±5% resistance=220 package=THT]
  R7 = Resistor [tolerance=±5% resistance=220 package=THT]
  R8 = Resistor [tolerance=±5% resistance=220 package=THT]
  R9 = Rotary Potentiometer (Small) [maximum_resistance=100kΩ package=THT]

nets:
  N1: LED1.cathode, R1.Pin_0
  N2: LED1.anode, Part1.D9_PWM
  N3: Part1.A0, R9.wiper
  N4: Part1.D8, LED2.anode
  N5: Part1.D2, LED8.anode
  N6: Part1.D3_PWM, LED7.anode
  N7: Part1.D4, LED6.anode
  N8: Part1.D5_PWM, LED5.anode
  N9: Part1.D6_PWM, LED4.anode
  N10: Part1.D7, LED3.anode
  N11: Part1.5V, R9.leg1, R9.leg2
  N12: Part1.GND, R1.Pin_1, R2.Pin_1, R3.Pin_1, R4.Pin_1, R5.Pin_1, R6.Pin_1, R7.Pin_1, R8.Pin_1
  N13: LED2.cathode, R2.Pin_0
  N14: LED3.cathode, R3.Pin_0
  N15: LED4.cathode, R4.Pin_0
  N16: LED5.cathode, R5.Pin_0
  N17: LED6.cathode, R6.Pin_0
  N18: LED7.cathode, R7.Pin_0
  N19: LED8.cathode, R8.Pin_0
