# Fritzing sketch 09 Dual Color LED (saved by Fritzing 0.9.2b)

parts:
  Part1 = Arduino Uno (Rev3)
  S1 = Dual-color led v1.0 [package=THT]

nets:
  N1: Part1.D10_PWM/SS, S1.R
  N2: Part1.D11_PWM/MOSI, S1.Y
  N3: Part1.GND, S1.G

custom parts:
  Dual-color led v1.0: Dual-color led v1.0 www.sunfounder.com
