# Fritzing sketch 10 RGB LED (saved by Fritzing 0.9.3b)
breadboards: 1

parts:
  Part1 = Arduino Uno (Rev3) - ICSP
  R1 = Resistor [tolerance=±5% resistance=220 package=THT]
  LED1 = RGB LED (com. cathode, rgb) [package="5 mm [THT]"]
  R2 = Resistor [tolerance=±5% resistance=220 package=THT]
  R3 = Resistor [tolerance=±5% resistance=220 package=THT]

nets:
  N1: Part1.D9_PWM, R3.Pin_1
  N2: Part1.D10_PWM/SS, R2.Pin_1
  N3: Part1.D11_PWM/MOSI, R1.Pin_1
  N4: Part1.GND, LED1.common_cathode
  N5: R1.Pin_0, LED1.red_anode
  N6: LED1.green_anode, R2.Pin_0
  N7: LED1.blue_anode, R3.Pin_0
