# Fritzing sketch 11 RGB LED Module (saved by Fritzing 0.9.3b)

parts:
  Part1 = Arduino Uno (Rev3)
  module1 = RGB LED

nets:
  N1: Part1.D9_PWM, module1.B
  N2: Part1.D10_PWM/SS, module1.G
  N3: Part1.D11_PWM/MOSI, module1.R
  5V: Part1.5V, module1.VCC

custom parts:
  RGB LED: RGB LED module of SunFounder Sensor Kit
