# Fritzing sketch 12 Autoflash LED (saved by Fritzing 0.9.3b)

parts:
  Part1 = Arduino Uno (Rev3)
  module2 = auto-flah led v1.0

nets:
  N1: Part1.5V, module2.S
  N2: Part1.GND, module2.-

custom parts:
  auto-flah led v1.0: auto-flash led v1.0 www.sunfounder.com
