# Fritzing sketch 14 Buzzer Module (saved by Fritzing 0.9.3b)

parts:
  Part1 = Arduino Uno (Rev3)
  module1 = Buzzer

nets:
  N1: Part1.D9_PWM, module1.SIG
  5V: Part1.5V, module1.VCC
  GND: Part1.GND, module1.GND

custom parts:
  Buzzer: buzzer module of SunFounder Sensor Kit
