# Fritzing sketch 16 4 Channel Relay Module (saved by Fritzing 0.9.3b)

parts:
  Part1 = Arduino Uno (Rev3)
  Part2 = 4-Channels Relay

nets:
  N1: Part1.D8, Part2.IN4
  N2: Part1.D9_PWM, Part2.IN3
  N3: Part1.D10_PWM/SS, Part2.IN2
  N4: Part1.D11_PWM/MOSI, Part2.IN1
  5V: Part1.5V, Part2.VCC
  GND: Part1.GND, Part2.GND
