# Fritzing sketch 17 Rotary Encoder Module (saved by Fritzing 0.9.3b)

parts:
  Part1 = Arduino Uno (Rev3)
  module2 = Rotary Encoder

nets:
  N1: Part1.D8, module2.CLK
  N2: Part1.D9_PWM, module2.DT
  N3: Part1.D10_PWM/SS, module2.SW
  5V: Part1.5V, module2.VCC
  GND: Part1.GND, module2.GND

custom parts:
  Rotary Encoder: Rotary Encoder module of SunFounder Sensor Kit
