# Fritzing sketch 18 555 Timer (saved by Fritzing 0.9.3b)
breadboards: 1

parts:
  Part1 = Arduino Uno (Rev3) - ICSP
  R1 = Rotary Potentiometer (Small) [maximum_resistance=100kΩ package=THT]
  R2 = Resistor [tolerance=±5% resistance=10k package=THT]
  U1 = 555 Timer [package="DIP8 [THT]"]
  C1 = Ceramic Capacitor [capacitance=100nF package="100 mil [THT, multilayer]"]
  C2 = Ceramic Capacitor [capacitance=100nF package="100 mil [THT, multilayer]"]

nets:
  N1: Part1.5V, R2.Pin_0, U1.Reset, U1.Vcc_Supply_Voltage
  N2: Part1.D9_PWM, U1.Output
  N3: Part1.GND, U1.Ground, C1.1, C2.0
  N4: R1.leg1, U1.Trigger, U1.Threshold, C2.1
  N5: R1.wiper, R2.Pin_1, U1.Discharge
  N6: U1.Control_Voltage, C1.0
