# Fritzing sketch 19 7 Segment Display (saved by Fritzing 0.9.3b)
breadboards: 1

parts:
  Part1 = Arduino Uno (Rev3) - ICSP
  DI1 = 7 Segment Display
  R1 = Resistor [tolerance=±5% resistance=220 package=THT]
  R2 = Resistor [tolerance=±5% resistance=220 package=THT]
  R3 = Resistor [tolerance=±5% resistance=220 package=THT]
  R4 = Resistor [tolerance=±5% resistance=220 package=THT]
  R5 = Resistor [tolerance=±5% resistance=220 package=THT]
  R6 = Resistor [tolerance=±5% resistance=220 package=THT]
  R7 = Resistor [tolerance=±5% resistance=220 package=THT]
  R8 = Resistor [tolerance=±5% resistance=220 package=THT]

nets:
  N1: Part1.D8, R5.Pin_0
  N2: Part1.D9_PWM, R6.Pin_0
  N3: Part1.D10_PWM/SS, R2.Pin_0
  N4: Part1.D11_PWM/MOSI, R1.Pin_0
  N5: Part1.D4, R4.Pin_1
  N6: Part1.D5_PWM, R3.Pin_1
  N7: Part1.D6_PWM, R8.Pin_1
  N8: Part1.D7, R7.Pin_1
  N9: Part1.GND, DI1.common_cathode
  N10: DI1.Segment_E, R2.Pin_1
  N11: DI1.Segment_D, R1.Pin_1
  N12: DI1.Segment_C, R3.Pin_0
  N13: DI1.Segment_DP, R4.Pin_0
  N14: DI1.Segment_B, R8.Pin_0
  N15: DI1.Segment_A, R7.Pin_0
  N16: DI1.Segment_F, R5.Pin_1
  N17: DI1.Segment_G, R6.Pin_1
