# Fritzing sketch 20 4 Digit 7 Segment Display (saved by Fritzing 0.9.3b)
breadboards: 1

parts:
  Part1 = Arduino Uno (Rev3) - ICSP
  R1 = Resistor [tolerance=±5% resistance=220 package=THT]
  R2 = Resistor [tolerance=±5% resistance=220 package=THT]
  R3 = Resistor [tolerance=±5% resistance=220 package=THT]
  R4 = Resistor [tolerance=±5% resistance=220 package=THT]
  R5 = Resistor [tolerance=±5% resistance=220 package=THT]
  R6 = Resistor [tolerance=±5% resistance=220 package=THT]
  R7 = Resistor [tolerance=±5% resistance=220 package=THT]
  R8 = Resistor [tolerance=±5% resistance=220 package=THT]
  LED4 = 7-SEGMENT-4DIGIT-YOUNGSUN [package=7-segment-4digit-youngsun-longpads]

nets:
  N1: Part1.D8, R4.Pin_1
  N2: Part1.D9_PWM, R3.Pin_1
  N3: Part1.D10_PWM/SS, LED4.DP
  N4: Part1.D11_PWM/MOSI, LED4.F
  N5: Part1.D12/MISO, LED4.COL-C
  N6: Part1.D13/SCK, LED4.G
  N7: Part1.D2, R8.Pin_0
  N8: Part1.D3_PWM, R6.Pin_1
  N9: Part1.D4, R5.Pin_1
  N10: Part1.D5_PWM, R2.Pin_0
  N11: Part1.D6_PWM, R1.Pin_0
  N12: Part1.D7, R7.Pin_0
  N13: R1.Pin_1, LED4.DIG2
  N14: R2.Pin_1, LED4.D
  N15: R3.Pin_0, LED4.COL-A
  N16: R4.Pin_0, LED4.DIG3
  N17: R5.Pin_0, LED4.E
  N18: R6.Pin_0, LED4.APOS-A
  N19: R7.Pin_1, LED4.C
  N20: R8.Pin_1, LED4.A

custom parts:
  7-SEGMENT-4DIGIT-YOUNGSUN: This is a part for the 4-Digit 7-segment LEDs from Young Sun. Different from the Digikey LEDs, all 16 pins are used. The LONGPADS Variant is used for a test jig, but you may like it because there is more pad to solder to. If you are concerned about routing space, the standard works just fine though.
