# Fritzing sketch 21 7 Segment 74HC595 (saved by Fritzing 0.9.3b)
breadboards: 1

parts:
  Part1 = Arduino Uno (Rev3) - ICSP
  R1 = Resistor [tolerance=±5% resistance=220 package=THT]
  R2 = Resistor [tolerance=±5% resistance=220 package=THT]
  R3 = Resistor [tolerance=±5% resistance=220 package=THT]
  R4 = Resistor [tolerance=±5% resistance=220 package=THT]
  R5 = Resistor [tolerance=±5% resistance=220 package=THT]
  R6 = Resistor [tolerance=±5% resistance=220 package=THT]
  R7 = Resistor [tolerance=±5% resistance=220 package=THT]
  R8 = Resistor [tolerance=±5% resistance=220 package=THT]
  U1 = 74HC595 [package="DIP16 [THT]"]
  DI1 = 7 Segment Display

nets:
  N1: Part1.D8, U1.SH_CP
  N2: Part1.D11_PWM/MOSI, U1.DS
  N3: Part1.D12/MISO, U1.ST_CP
  5V: Part1.5V, U1.MR, U1.VCC
  GND: Part1.GND, U1.GND, U1.OE, DI1.common_anode
  N4: R1.Pin_0, U1.Q4
  N5: R1.Pin_1, DI1.Segment_D
  N6: R2.Pin_0, U1.Q3
  N7: R2.Pin_1, DI1.Segment_E
  N8: R3.Pin_0, DI1.Segment_C
  N9: R3.Pin_1, U1.Q5
  N10: R4.Pin_0, DI1.Segment_DP
  N11: R4.Pin_1, U1.Q0
  N12: R5.Pin_0, U1.Q2
  N13: R5.Pin_1, DI1.Segment_F
  N14: R6.Pin_0, U1.Q1
  N15: R6.Pin_1, DI1.Segment_G
  N16: R7.Pin_0, DI1.Segment_A
  N17: R7.Pin_1, U1.Q7
  N18: R8.Pin_0, DI1.Segment_B
  N19: R8.Pin_1, U1.Q6
