# Fritzing sketch 22 4 Digit 7 Segment 74HC595 (saved by Fritzing 0.9.3b)
breadboards: 1

parts:
  Part1 = Arduino Uno (Rev3) - ICSP
  R1 = Resistor [tolerance=±5% resistance=220 package=THT]
  R2 = Resistor [tolerance=±5% resistance=220 package=THT]
  R3 = Resistor [tolerance=±5% resistance=220 package=THT]
  R4 = Resistor [tolerance=±5% resistance=220 package=THT]
  R5 = Resistor [tolerance=±5% resistance=220 package=THT]
  R6 = Resistor [tolerance=±5% resistance=220 package=THT]
  R7 = Resistor [tolerance=±5% resistance=220 package=THT]
  R8 = Resistor [tolerance=±5% resistance=220 package=THT]
  U1 = 74HC595 [package="DIP16 [THT]"]
  LED1 = 7-SEGMENT-4DIGIT-YOUNGSUN [package=7-segment-4digit-youngsun-longpads]
  R9 = Resistor [tolerance=±5% resistance=220 package=THT]
  R10 = Resistor [tolerance=±5% resistance=220 package=THT]
  R11 = Resistor [tolerance=±5% resistance=220 package=THT]
  R12 = Resistor [tolerance=±5% resistance=220 package=THT]
  U2 = 74HC595 [package="DIP16 [THT]"]

nets:
  N1: Part1.D8, U1.SH_CP, U2.SH_CP
  N2: Part1.D11_PWM/MOSI, U1.DS
  N3: Part1.D12/MISO, U1.ST_CP, U2.ST_CP
  VCC: Part1.5V, U1.MR, U1.VCC, U2.MR, U2.VCC
  GND: Part1.GND, U1.GND, U1.OE, U2.GND
  N4: R1.Pin_0, LED1.DIG3
  N5: R1.Pin_1, U2.Q2
  N6: R2.Pin_0, U1.Q1
  N7: R2.Pin_1, LED1.A
  N8: R3.Pin_0, LED1.DP
  N9: R3.Pin_1, U2.Q3
  N10: R4.Pin_0, U1.Q0
  N11: R4.Pin_1, LED1.G
  N12: R5.Pin_0, LED1.DIG2
  N13: R5.Pin_1, U1.Q6
  N14: R6.Pin_0, LED1.E
  N15: R6.Pin_1, U2.Q1
  N16: R7.Pin_0, LED1.D
  N17: R7.Pin_1, U1.Q7
  N18: R8.Pin_0, LED1.COL-A
  N19: R8.Pin_1, U2.Q0
  N20: U1.Q2, R9.Pin_0
  N21: U1.Q3, R11.Pin_0
  N22: U1.Q4, R12.Pin_0
  N23: U1.Q5, R10.Pin_0
  N24: U1.Q7', U2.DS
  N25: LED1.APOS-A, R10.Pin_1
  N26: LED1.F, R12.Pin_1
  N27: LED1.COL-C, R11.Pin_1
  N28: LED1.C, R9.Pin_1

custom parts:
  7-SEGMENT-4DIGIT-YOUNGSUN: This is a part for the 4-Digit 7-segment LEDs from Young Sun. Different from the Digikey LEDs, all 16 pins are used. The LONGPADS Variant is used for a test jig, but you may like it because there is more pad to solder to. If you are concerned about routing space, the standard works just fine though.
