# Fritzing sketch 23 LED 74HC595 (saved by Fritzing 0.9.3b)
breadboards: 1

parts:
  Part1 = Arduino Uno (Rev3) - ICSP
  R6 = Resistor [tolerance=±5% resistance=220 package=THT]
  U1 = 74HC595 [package="DIP16 [THT]"]
  R7 = Resistor [tolerance=±5% resistance=220 package=THT]
  R8 = Resistor [tolerance=±5% resistance=220 package=THT]
  R9 = Resistor [tolerance=±5% resistance=220 package=THT]
  R10 = Resistor [tolerance=±5% resistance=220 package=THT]
  R11 = Resistor [tolerance=±5% resistance=220 package=THT]
  R12 = Resistor [tolerance=±5% resistance=220 package=THT]
  R13 = Resistor [tolerance=±5% resistance=220 package=THT]
  LED1 = LED - 5mm [color="Red (633nm)" package="5 mm [THT]"]
  LED2 = LED - 5mm [color="Red (633nm)" package="5 mm [THT]"]
  LED3 = LED - 5mm [color="Red (633nm)" package="5 mm [THT]"]
  LED4 = LED - 5mm [color="Red (633nm)" package="5 mm [THT]"]
  LED5 = LED - 5mm [color="Red (633nm)" package="5 mm [THT]"]
  LED6 = LED - 5mm [color="Red (633nm)" package="5 mm [THT]"]
  LED7 = LED - 5mm [color="Red (633nm)" package="5 mm [THT]"]
  LED8 = LED - 5mm [color="Red (633nm)" package="5 mm [THT]"]

nets:
  N1: Part1.D8, U1.SH_CP
  N2: Part1.D11_PWM/MOSI, U1.DS
  N3: Part1.D12/MISO, U1.ST_CP
  5V: Part1.5V, U1.MR, U1.VCC
  GND: Part1.GND, R6.Pin_0, U1.GND, U1.OE, R7.Pin_0, R8.Pin_0, R9.Pin_0, R10.Pin_0, R11.Pin_0, R12.Pin_0, R13.Pin_0
  N4: R6.Pin_1, LED2.cathode
  N5: U1.Q1, LED2.anode
  N6: U1.Q2, LED3.anode
  N7: U1.Q3, LED4.anode
  N8: U1.Q4, LED5.anode
  N9: U1.Q5, LED6.anode
  N10: U1.Q6, LED7.anode
  N11: U1.Q7, LED8.anode
  N12: U1.Q0, LED1.anode
  N13: R7.Pin_1, LED6.cathode
  N14: R8.Pin_1, LED5.cathode
  N15: R9.Pin_1, LED1.cathode
  N16: R10.Pin_1, LED3.cathode
  N17: R11.Pin_1, LED8.cathode
  N18: R12.Pin_1, LED4.cathode
  N19: R13.Pin_1, LED7.cathode
