# Fritzing sketch 24 Dot Matrix 74HC595 (saved by Fritzing 0.9.3b)
breadboards: 1

parts:
  Part1 = Arduino Uno (Rev3) - ICSP
  R1 = Resistor [tolerance=±5% resistance=220 package=THT]
  R2 = Resistor [tolerance=±5% resistance=220 package=THT]
  R3 = Resistor [tolerance=±5% resistance=220 package=THT]
  R4 = Resistor [tolerance=±5% resistance=220 package=THT]
  U1 = 74HC595 [package="DIP16 [THT]"]
  R9 = Resistor [tolerance=±5% resistance=220 package=THT]
  R10 = Resistor [tolerance=±5% resistance=220 package=THT]
  R11 = Resistor [tolerance=±5% resistance=220 package=THT]
  R12 = Resistor [tolerance=±5% resistance=220 package=THT]
  U2 = 74HC595 [package="DIP16 [THT]"]
  module2 = 788BS Dot matix

nets:
  N1: Part1.D8, U1.SH_CP, U2.SH_CP
  N2: Part1.D11_PWM/MOSI, U1.DS
  N3: Part1.D12/MISO, U1.ST_CP, U2.ST_CP
  VCC: Part1.5V, U1.MR, U1.VCC, U2.MR, U2.VCC
  GND: Part1.GND, U1.GND, U1.OE, U2.GND
  N4: R1.Pin_0, U1.Q7
  N5: R1.Pin_1, module2.P9
  N6: R2.Pin_0, U1.Q4
  N7: R2.Pin_1, module2.P12
  N8: R3.Pin_0, U1.Q6
  N9: R3.Pin_1, module2.P14
  N10: R4.Pin_0, module2.P8
  N11: R4.Pin_1, U1.Q5
  N12: U1.Q1, R12.Pin_1
  N13: U1.Q2, R11.Pin_1
  N14: U1.Q3, R9.Pin_1
  N15: U1.Q7', U2.DS
  N16: U1.Q0, R10.Pin_1
  N17: R9.Pin_0, module2.P1
  N18: R10.Pin_0, module2.P5
  N19: R11.Pin_0, module2.P7
  N20: R12.Pin_0, module2.P2
  N21: U2.Q1, module2.P3
  N22: U2.Q2, module2.P4
  N23: U2.Q3, module2.P10
  N24: U2.Q4, module2.P6
  N25: U2.Q5, module2.P11
  N26: U2.Q6, module2.P15
  N27: U2.Q7, module2.P16
  N28: U2.Q0, module2.P13

custom parts:
  788BS Dot matix: 788BS 8x8 dot matix from SunFounder
