# Fritzing sketch 29 LCD 1602 (saved by Fritzing 0.9.3b)
breadboards: 1

parts:
  Part1 = Arduino Uno (Rev3) - ICSP
  LCD1 = LCD screen
  R1 = Rotary Potentiometer (Small) [maximum_resistance=100kΩ package=THT]

nets:
  GND: Part1.GND, LCD1.VSS, LCD1.R/W, LCD1.LED-, R1.leg2
  N1: Part1.D10_PWM/SS, LCD1.DB4
  N2: Part1.D11_PWM/MOSI, LCD1.DB5
  N3: Part1.D12/MISO, LCD1.DB6
  N4: Part1.D13/SCK, LCD1.DB7
  N5: Part1.D4, LCD1.RS
  N6: Part1.D6_PWM, LCD1.E
  3V3: Part1.3V3, LCD1.VDD
  N7: Part1.5V, LCD1.LED+, R1.leg1
  N8: LCD1.V0, R1.wiper
