# Fritzing sketch 31 Joystick PS2 (saved by Fritzing 0.9.3b)

parts:
  Part1 = Arduino Uno (Rev3)
  module1 = JoyStick

nets:
  N1: Part1.A0, module1.X
  N2: Part1.A1, module1.Y
  N3: Part1.D7, module1.BT
  5V: Part1.5V, module1.VCC
  GND: Part1.GND, module1.GND

custom parts:
  JoyStick: JoyStick module of SunFounder Sensor Kit
