# Fritzing sketch 36 RFID (saved by Fritzing 0.9.3b)

parts:
  Part1 = Arduino Uno (Rev3)
  module1 = RFID-RC522

nets:
  N1: Part1.D2, module1.RST
  N2: Part1.D3_PWM, module1.MISO
  N3: Part1.D4, module1.MOSI
  N4: Part1.D5_PWM, module1.SCK
  N5: Part1.D6_PWM, module1.NSS
  3V3: Part1.3V3, module1.VCC
  GND: Part1.GND, module1.GND

custom parts:
  RFID-RC522: RFID-RC522 module from Sunfounder
