# Fritzing sketch 40 Switch Hall (saved by Fritzing 0.9.3b)

parts:
  Part1 = Arduino Uno (Rev3)
  S1 = Switch Hall Sensor v1.0 [package=THT]

nets:
  N1: Part1.D8, S1.Y
  N2: Part1.5V, S1.R
  N3: Part1.GND, S1.G

custom parts:
  Switch Hall Sensor v1.0: Switch Hall Sensor v1.0 www.sunfounder.com
