# Fritzing sketch 41 Analog Hall (saved by Fritzing 0.9.3b)

parts:
  Part1 = Arduino Uno (Rev3)
  module1 = Hall

nets:
  N1: Part1.A0, module1.AO
  N2: Part1.D8, module1.DO
  5V: Part1.5V, module1.VCC
  GND: Part1.GND, module1.GND

custom parts:
  Hall: Hall sensor module of SunFounder Sensor Kit
