# Fritzing sketch 42 Shock (saved by Fritzing 0.9.3b)

parts:
  Part1 = Arduino Uno (Rev3)
  S1 = Shock Switch v1.0 [package=THT]

nets:
  N1: Part1.D8, S1.S
  N2: Part1.5V, S1.+
  N3: Part1.GND, S1.-

custom parts:
  Shock Switch v1.0: Shock Switch v1.0 www.sunfounder.com
