# Fritzing sketch 43 Knock (saved by Fritzing 0.9.3b)

parts:
  Part1 = Arduino Uno (Rev3)
  module1 = Vibration Switch

nets:
  N1: Part1.D8, module1.SIG
  5V: Part1.5V, module1.VCC
  GND: Part1.GND, module1.GND
