# Fritzing sketch 45 IR R (saved by Fritzing 0.9.3b)

parts:
  Part1 = Arduino Uno (Rev3)
  module3 = Infrared-Receiver

nets:
  N1: Part1.D9_PWM, module3.SIG
  5V: Part1.5V, module3.VCC
  GND: Part1.GND, module3.GND

custom parts:
  Infrared-Receiver: Infrared-Receiver module of SunFounder Sensor Kit
