# Fritzing sketch 46 Laser (saved by Fritzing 0.9.3b)

parts:
  Part1 = Arduino Uno (Rev3)
  S1 = Laser Transmitter v1.0 [package=THT]

nets:
  N1: Part1.D9_PWM, S1.S
  N2: Part1.5V, S1.+
  N3: Part1.GND, S1.-

custom parts:
  Laser Transmitter v1.0: A laser is a device that emits light through a process of optical amplification based on the stimulated emission of electromagnetic radiation. Lasers differ from other sources of light because they emit light coherently.
