# Fritzing sketch 47 Reed Switch (saved by Fritzing 0.9.3b)

parts:
  Part1 = Arduino Uno (Rev3)
  S1 = Mini Reed v1.0 [package=THT]

nets:
  N1: Part1.D9_PWM, S1.S
  N2: Part1.5V, S1.+
  N3: Part1.GND, S1.-

custom parts:
  Mini Reed v1.0: A reed switch is a type of line switch component that realizes control by magnetic signals
