# Fritzing sketch 49 Photo Interrupter (saved by Fritzing 0.9.3b)

parts:
  Part1 = Arduino Uno (Rev3)
  module2 = Photo-interrupter

nets:
  N1: Part1.D9_PWM, module2.SIG
  5V: Part1.5V, module2.VCC
  GND: Part1.GND, module2.GND

custom parts:
  Photo-interrupter: Photo-interrupter module of SunFounder Sensor Kit
