# Fritzing sketch 4N35 (saved by Fritzing 0.9.3b)
breadboards: 1

parts:
  Part1 = Arduino Uno (Rev3)
  U1 = Optocoupler [package=THT]
  LED1 = LED - 5mm [color="Red (633nm)" package="5 mm [THT]"]
  R1 = Resistor [tolerance=±5% resistance=220 package=THT]
  R2 = Resistor [tolerance=±5% resistance=1k package=THT]

nets:
  N1: Part1.D9_PWM, U1.Pin_2
  N2: Part1.5V, R1.Pin_1, R2.Pin_0
  N3: Part1.GND, U1.Pin_4
  N4: U1.Pin_1, R2.Pin_1
  N5: U1.Pin_5, LED1.cathode
  N6: LED1.anode, R1.Pin_0
