# Fritzing sketch 52 Mercury (saved by Fritzing 0.9.3b)

parts:
  Part1 = Arduino Uno (Rev3)
  module4 = Mercury Switch

nets:
  N1: Part1.D9_PWM, module4.SIG
  5V: Part1.5V, module4.VCC
  GND: Part1.GND, module4.GND

custom parts:
  Mercury Switch: Mercury Switch module of SunFounder Sensor Kit
