# Fritzing sketch 54 Photoresistor Module (saved by Fritzing 0.9.3b)

parts:
  Part1 = Arduino Uno (Rev3)
  module5 = Photoresistor

nets:
  N1: Part1.A0, module5.SIG
  5V: Part1.5V, module5.VCC
  GND: Part1.GND, module5.GND

custom parts:
  Photoresistor: Photoresistor module of SunFounder Sensor Kit
