# Fritzing sketch 55 Humiture (saved by Fritzing 0.9.3b)

parts:
  Part1 = Arduino Uno (Rev3)
  module6 = DHT11 Humiture Sensor

nets:
  N1: Part1.A0, module6.SIG
  5V: Part1.5V, module6.VCC
  GND: Part1.GND, module6.GND

custom parts:
  DHT11 Humiture Sensor: DHT11 Humiture Sensor module of SunFounder Sensor Kit
