# Fritzing sketch 56 Obstacle (saved by Fritzing 0.9.3b)

parts:
  Part1 = Arduino Uno (Rev3)
  module7 = IR Obstacle

nets:
  N1: Part1.A0, module7.SIG
  5V: Part1.5V, module7.VCC
  GND: Part1.GND, module7.GND

custom parts:
  IR Obstacle: IR Obstacle module of SunFounder Sensor Kit.
