# Fritzing sketch 57 Tracking (saved by Fritzing 0.9.3b)

parts:
  Part1 = Arduino Uno (Rev3)
  module8 = Tracking

nets:
  N1: Part1.A0, module8.SIG
  5V: Part1.5V, module8.VCC
  GND: Part1.GND, module8.GND

custom parts:
  Tracking: Tracking module of SunFounder Sensor Kit
