# Fritzing sketch 58 Voice (saved by Fritzing 0.9.3b)

parts:
  Part1 = Arduino Uno (Rev3)
  module9 = sound sensor-v1.0

nets:
  N1: Part1.A0, module9.A0
  N2: Part1.D9_PWM, module9.D0
  N3: Part1.5V, module9.G
  N4: Part1.GND, module9.+

custom parts:
  sound sensor-v1.0: sound sensor-v1.0 module
