# Fritzing sketch 59 Metal Touch (saved by Fritzing 0.9.3b)

parts:
  Part1 = Arduino Uno (Rev3)
  module10 = Linear Hall Sensor(lm393)-V1.0

nets:
  N1: Part1.A0, module10.AO
  N2: Part1.D9_PWM, module10.DO
  N3: Part1.5V, module10.G
  N4: Part1.GND, module10.+

custom parts:
  Linear Hall Sensor(lm393)-V1.0: Linear Hall Sensor(lm393)-V1.0 www.sunfounder.com
