# Fritzing sketch 60 Flame (saved by Fritzing 0.9.3b)

parts:
  Part1 = Arduino Uno (Rev3)
  module11 = Flame Sensor

nets:
  N1: Part1.A0, module11.AO
  N2: Part1.D9_PWM, module11.DO
  5V: Part1.5V, module11.VCC
  GND: Part1.GND, module11.GND

custom parts:
  Flame Sensor: Flame Sensor module of SunFounder Sensor Kit
