# Fritzing sketch 61 Gas (saved by Fritzing 0.9.3b)

parts:
  Part1 = Arduino Uno (Rev3)
  module12 = MQ-2 Gas Sensor

nets:
  N1: Part1.A0, module12.AO
  N2: Part1.D9_PWM, module12.DO
  5V: Part1.5V, module12.VCC
  GND: Part1.GND, module12.GND

custom parts:
  MQ-2 Gas Sensor: MQ-2 Gas Sensor module of SunFounder Sensor Kit
