# Fritzing sketch 62 Rain (saved by Fritzing 0.9.3b)

parts:
  Part1 = Arduino Uno (Rev3)
  module13 = Rain Detection board
  module14 = LM393

nets:
  N1: Part1.A0, module14.AO
  N2: Part1.D9_PWM, module14.DO
  5V: Part1.5V, module14.VCC
  N3: Part1.GND, module14.GND#8
  N4: module13.+, module14.GND#10
  N5: module13.-, module14.IN

custom parts:
  Rain Detection board: Rain Detection board for SunFounder Sensor Kit (along with LM393).
  LM393: LM393 module of SunFounder Sensor Kit
