# Fritzing sketch 63 Ultrasonic (saved by Fritzing 0.9.3b)

parts:
  Part1 = Arduino Uno (Rev3)
  module1 = Ultrasonic-HC-SRO4

nets:
  N1: Part1.D8, module1.TRIG
  N2: Part1.D9_PWM, module1.ECHO
  5V: Part1.5V, module1.VCC
  GND: Part1.GND, module1.GND

custom parts:
  Ultrasonic-HC-SRO4: The ultrasonic sensor uses sound to accurately detect objects and measure distances. It sends out ultrasonic waves and converts them into electronic signals
