# Fritzing sketch 64 Barometer (saved by Fritzing 0.9.3b)

parts:
  Part1 = Arduino Uno (Rev3)
  module1 = Barometer

nets:
  N1: Part1.A4/SDA, module1.SDA
  N2: Part1.A5/SCL, module1.SCL
  5V: Part1.5V, module1.VCC
  GND: Part1.GND, module1.GND

custom parts:
  Barometer: barometer module of SunFounder Sensor Kit
