# Fritzing sketch 65 RTC (saved by Fritzing 0.9.3b)

parts:
  Part1 = Arduino Uno (Rev3)
  module1 = DS1302 RTC

nets:
  N1: Part1.D5_PWM, module1.RST
  N2: Part1.D6_PWM, module1.SDA
  N3: Part1.D7, module1.SCL
  5V: Part1.5V, module1.VCC
  GND: Part1.GND, module1.GND

custom parts:
  DS1302 RTC: DS1302RTC module of SunFounder Sensor Kit
