# Fritzing sketch 66 Color (saved by Fritzing 0.9.3b)

parts:
  Part1 = Arduino Uno (Rev3)
  module1 = Color Seneor

nets:
  N1: Part1.D2, module1.OUT
  N2: Part1.D3_PWM, module1.S0
  N3: Part1.D4, module1.S1
  N4: Part1.D5_PWM, module1.S2
  N5: Part1.D6_PWM, module1.S3
  5V: Part1.5V, module1.VCC
  GND: Part1.GND, module1.GND

custom parts:
  Color Seneor: Color Sensor of SunFounder Sensor Kit for Arduino
