# Fritzing sketch 67 Liquid (saved by Fritzing 0.9.3b)

parts:
  Part1 = Arduino Uno (Rev3)
  module1 = Water sensor

nets:
  N1: Part1.A0, module1.S
  N2: Part1.5V, module1.+
  N3: Part1.GND, module1.-

custom parts:
  Water sensor: Water sensor module of SunFounder Sensor Kit
