# Fritzing sketch 69 ATemp (saved by Fritzing 0.9.3b)

parts:
  Part1 = Arduino Uno (Rev3)
  module1 = Thermistor Module (lm393)-V1.0

nets:
  N1: Part1.A0, module1.A0
  N2: Part1.D9_PWM, module1.D0
  N3: Part1.5V, module1.+
  N4: Part1.GND, module1.G

custom parts:
  Thermistor Module (lm393)-V1.0: www.sunfounder.com
