# Fritzing sketch 70 DS18B20 (saved by Fritzing 0.9.3b)

parts:
  Part1 = Arduino Uno (Rev3)
  module1 = DS18B20 module

nets:
  N1: Part1.D9_PWM, module1.SIG
  5V: Part1.5V, module1.VCC
  GND: Part1.GND, module1.GND

custom parts:
  DS18B20 module: DS18B20 module from SunFounder Sensor Kit
