# Fritzing sketch 73 MPU6050 (saved by Fritzing 0.9.3b)

parts:
  Part1 = Arduino Uno (Rev3)
  module1 = MPU6050

nets:
  N1: Part1.A4/SDA, module1.SDA
  N2: Part1.A5/SCL, module1.SCL
  3V3: Part1.3V3, module1.VCC
  GND: Part1.GND, module1.GND

custom parts:
  MPU6050: MPU6050 Gyro Acceleration module of SunFounder Sensor Kit
