# Fritzing sketch DC Motor (saved by Fritzing 0.9.3b)
breadboards: 1

parts:
  Part1 = Arduino Uno (Rev3)
  IC1 = L293D [package=THT]
  M1 = DC Motor

nets:
  N1: Part1.D9_PWM, IC1.In_2
  N2: Part1.D10_PWM/SS, IC1.In_1
  N3: Part1.5V, IC1.Enable_1, IC1.+Vmotor, IC1.+V
  N4: Part1.GND, IC1.0V
  N5: IC1.Out_1_(_Controlled_by_Enable_1_), M1.pin_2
  N6: IC1.Out_2_(_Controlled_by_Enable_1_), M1.pin_1
