# Fritzing sketch Dot Matrix MCU (saved by Fritzing 0.9.3b)

parts:
  Part1 = Arduino Uno (Rev3)
  Part2 = Matrix LED de 8x8 basada en MAX7219

nets:
  N1: Part1.D10_PWM/SS, Part2.CS
  N2: Part1.D11_PWM/MOSI, Part2.CLK
  N3: Part1.D12/MISO, Part2.DIN
  5V: Part1.5V, Part2.VCC
  GND: Part1.GND, Part2.GND
