# Fritzing sketch Keypad (saved by Fritzing 0.9.3b)

parts:
  Part1 = Arduino Uno (Rev3)
  module1 = KeyPad

nets:
  N1: Part1.D8, module1.X1
  N2: Part1.D9_PWM, module1.X2
  N3: Part1.D10_PWM/SS, module1.X3
  N4: Part1.D11_PWM/MOSI, module1.X4
  N5: Part1.D4, module1.Y1
  N6: Part1.D5_PWM, module1.Y2
  N7: Part1.D6_PWM, module1.Y3
  N8: Part1.D7, module1.Y4

custom parts:
  KeyPad: Keypad module by Sunfounder
