# Fritzing sketch LCD 2004 (saved by Fritzing 0.9.3b)
breadboards: 1

parts:
  Part1 = Arduino Uno (Rev3) - ICSP
  R1 = Rotary Potentiometer (Small) [maximum_resistance=100kΩ package=THT]
  LCD2 = LCD 20x04

nets:
  N1: Part1.D10_PWM/SS, LCD2.DB4
  N2: Part1.D11_PWM/MOSI, LCD2.DB5
  N3: Part1.D12/MISO, LCD2.DB6
  N4: Part1.D13/SCK, LCD2.DB7
  N5: Part1.D4, LCD2.RS
  N6: Part1.D6_PWM, LCD2.E
  3V3: Part1.3V3, LCD2.VDD
  N7: Part1.5V, R1.leg1, LCD2.LED+
  GND: Part1.GND, R1.leg2, LCD2.VSS, LCD2.R/W, LCD2.LED-
  N8: R1.wiper, LCD2.V0

custom parts:
  LCD 20x04: LCD 2004 character display, 4x rows of 20x characters. Blue.
