# Fritzing sketch Membrane Keypad (saved by Fritzing 0.9.3b)

parts:
  Part1 = Arduino Uno (Rev3)
  KEYPAD1 = Membrane Matrix Keypad

nets:
  N1: Part1.D8, KEYPAD1.4
  N2: Part1.D9_PWM, KEYPAD1.3
  N3: Part1.D10_PWM/SS, KEYPAD1.2
  N4: Part1.D11_PWM/MOSI, KEYPAD1.1
  N5: Part1.D5_PWM, KEYPAD1.7
  N6: Part1.D6_PWM, KEYPAD1.6
  N7: Part1.D7, KEYPAD1.5

custom parts:
  Membrane Matrix Keypad: Membrane Matrix 3x4 Keypad
