# Fritzing sketch NRF24L01 (saved by Fritzing 0.9.3b)
breadboards: 2

parts:
  Part1 = Arduino Uno (Rev3)
  Part2 = Arduino Uno (Rev3)
  LED1 = LED - 5mm [color="Red (633nm)" package="5 mm [THT]"]
  R1 = Resistor [tolerance=±5% resistance=220 package=THT]
  S1 = Pushbutton [package="[THT]"]
  R2 = Resistor [tolerance=±5% resistance=10k package=THT]
  Part3 = NRF24L01+ Breakout Board
  Part4 = NRF24L01+ Breakout Board

nets:
  N1: Part1.D9_PWM, S1.Pin_3, S1.Pin_4, R2.Pin_0
  N2: Part1.D2, Part3.CE
  N3: Part1.D3_PWM, Part3.SCK
  N4: Part1.D4, Part3.MISO
  N5: Part1.D5_PWM, Part3.CS
  N6: Part1.D6_PWM, Part3.MOSI
  N7: Part1.D7, Part3.IRQ
  5V: Part1.5V, S1.Pin_1, S1.Pin_2, Part3.VCC
  GND: Part1.GND, R2.Pin_1, Part3.GND
  N8: Part2.D9_PWM, LED1.anode
  N9: Part2.D2, Part4.CE
  N10: Part2.D3_PWM, Part4.SCK
  N11: Part2.D4, Part4.MISO
  N12: Part2.D5_PWM, Part4.CS
  N13: Part2.D6_PWM, Part4.MOSI
  N14: Part2.D7, Part4.IRQ
  GND_2: Part2.GND, R1.Pin_0, Part4.GND
  N15: LED1.cathode, R1.Pin_1
