# Fritzing sketch Relay (saved by Fritzing 0.9.3b)
breadboards: 1

parts:
  Part1 = Arduino Uno (Rev3)
  Q1 = TRANSISTOR_NPN [package=to-92-ammo]
  D1 = Rectifier Diode [part_number=1N4001 package="Melf DO-213 AB [SMD]"]
  R1 = Resistor [tolerance=±5% resistance=1k package="2010 [SMD]"]
  R2 = Resistor [tolerance=±5% resistance=220 package="2010 [SMD]"]
  LED1 = LED - 5mm [color="Red (633nm)" package="5 mm [THT]"]
  OMRON1 = OMRON PCB Power Relay – G5LE [part_number="G5LE-1\n" package=THT]

nets:
  N1: Part1.D9_PWM, R1.Pin_1
  N2: Part1.GND, Q1.E, LED1.cathode, OMRON1.C
  N3: Part1.5V, R2.Pin_0
  N4: Q1.B, R1.Pin_0
  N5: Q1.C, D1.cathode
  N6: D1.anode, OMRON1.COIL2
  N7: R2.Pin_1, LED1.anode
