# Fritzing sketch Stepper Motor (saved by Fritzing 0.9.3b)

parts:
  Part1 = Arduino Uno (Rev3)
  module1 = Step Motor
  module2 = Stepper Motor Driver

nets:
  N1: Part1.D9_PWM, module2.A
  N2: Part1.D10_PWM/SS, module2.B
  N3: Part1.D11_PWM/MOSI, module2.C
  N4: Part1.D12/MISO, module2.D
  5V: Part1.5V, module2.VCC
  GND: Part1.GND, module2.GND
  N5: module1.yellow, module2.OUT3
  N6: module1.orange, module2.OUT4
  N7: module1.red, module2.COM
  N8: module1.pink, module2.OUT2
  N9: module1.blue, module2.OUT1

custom parts:
  Step Motor: step motor
  Stepper Motor Driver: Stepper Motor Driver of SunFounder Sensor Kit for Arduino
