# Fritzing sketch 02 Button LED (saved by Fritzing 0.9.3b)
breadboards: 1

parts:
  LED1 = LED - 5mm [color="Red (633nm)" package="5 mm [THT]"]
  T-Cobbler1 = T-Cobbler
  R1 = Resistor [tolerance=±5% resistance=220 package=THT]
  S1 = Pushbutton [package="[THT]"]

nets:
  N1: LED1.cathode, T-Cobbler1.GPIO17
  N2: LED1.anode, R1.Pin_1
  N3: T-Cobbler1.3V3#0, R1.Pin_0
  N4: T-Cobbler1.GND#22, S1.Pin_1, S1.Pin_2
  N5: T-Cobbler1.GPIO18, S1.Pin_3, S1.Pin_4

custom parts:
  T-Cobbler: T-Cobbler for RPi B+ and Rpi2 from SunFounder
