# Fritzing sketch 04 Slide Switch LED (saved by Fritzing 0.9.3b)
breadboards: 1

parts:
  LED1 = LED - 5mm [color="Red (633nm)" package="5 mm [THT]"]
  T-Cobbler1 = T-Cobbler
  R1 = Resistor [tolerance=±5% resistance=220 package=THT]
  S1 = Toggle Switch [package=THT]

nets:
  N1: LED1.cathode, T-Cobbler1.GPIO17
  N2: LED1.anode, R1.Pin_1
  N3: T-Cobbler1.3V3#0, R1.Pin_0, S1.L2
  N4: T-Cobbler1.GND#22, S1.L1
  N5: T-Cobbler1.GPIO18, S1.COM

custom parts:
  T-Cobbler: T-Cobbler for RPi B+ and Rpi2 from SunFounder
