# Fritzing sketch 05 Pot LED (saved by Fritzing 0.9.2b)
breadboards: 1

parts:
  LED1 = LED - 5mm [color="Red (633nm)" package="5 mm [THT]"]
  T-Cobbler1 = T-Cobbler
  R1 = Resistor [tolerance=±5% resistance=220 package=THT]
  R2 = Rotary Potentiometer (Small) [maximum_resistance=100kΩ package=THT]
  module1 = PCF8591

nets:
  N1: LED1.cathode, T-Cobbler1.GPIO17
  N2: LED1.anode, R1.Pin_1
  N3: T-Cobbler1.3V3#0, R1.Pin_0, R2.leg1, module1.VCC
  N4: T-Cobbler1.SDA1, module1.SDA
  N5: T-Cobbler1.SCL1, module1.SCL
  N6: T-Cobbler1.GND#22, R2.leg2, module1.GND
  N7: R2.wiper, module1.AIN0

custom parts:
  T-Cobbler: T-Cobbler for RPi B+ and Rpi2 from SunFounder
  PCF8591: PCF8591 ADC module for SunFounder Sensor Kit
