# Fritzing sketch 07 Flowing LEDs (saved by Fritzing 0.9.2b)
breadboards: 1

parts:
  LED1 = LED - 5mm [color="Red (633nm)" package="5 mm [THT]"]
  T-Cobbler1 = T-Cobbler
  R1 = Resistor [tolerance=±5% resistance=220 package=THT]
  R2 = Resistor [tolerance=±5% resistance=220 package=THT]
  LED2 = LED - 5mm [color="Yellow (585nm)" package="5 mm [THT]"]
  R3 = Resistor [tolerance=±5% resistance=220 package=THT]
  LED3 = LED - 5mm [color="Green (560nm)" package="5 mm [THT]"]
  R4 = Resistor [tolerance=±5% resistance=220 package=THT]
  LED4 = LED - 5mm [color="White (6500K)" package="5 mm [THT]"]
  R5 = Resistor [tolerance=±5% resistance=220 package=THT]
  LED5 = LED - 5mm [color="Red (633nm)" package="5 mm [THT]"]
  R6 = Resistor [tolerance=±5% resistance=220 package=THT]
  LED6 = LED - 5mm [color="Yellow (585nm)" package="5 mm [THT]"]
  R7 = Resistor [tolerance=±5% resistance=220 package=THT]
  LED7 = LED - 5mm [color="Green (560nm)" package="5 mm [THT]"]
  R8 = Resistor [tolerance=±5% resistance=220 package=THT]
  LED8 = smd LED [color="White (6500K)" package="0603 [SMD]"]

nets:
  N1: LED1.cathode, T-Cobbler1.GPIO4
  N2: LED1.anode, R1.Pin_1
  N3: T-Cobbler1.3V3#0, R1.Pin_0, R2.Pin_0, R3.Pin_0, R4.Pin_0, R5.Pin_0, R6.Pin_0, R7.Pin_0, R8.Pin_0
  N4: T-Cobbler1.GPIO17, LED2.cathode
  N5: T-Cobbler1.GPIO27, LED3.cathode
  N6: T-Cobbler1.GPIO22, LED4.cathode
  N7: T-Cobbler1.GPIO18, LED5.cathode
  N8: T-Cobbler1.GPIO23, LED6.cathode
  N9: T-Cobbler1.GPIO24, LED7.cathode
  N10: T-Cobbler1.GPIO25, LED8.cathode
  N11: R2.Pin_1, LED2.anode
  N12: R3.Pin_1, LED3.anode
  N13: R4.Pin_1, LED4.anode
  N14: R5.Pin_1, LED5.anode
  N15: R6.Pin_1, LED6.anode
  N16: R7.Pin_1, LED7.anode
  N17: R8.Pin_1, LED8.anode

custom parts:
  T-Cobbler: T-Cobbler for RPi B+ and Rpi2 from SunFounder
