# Fritzing sketch 09 Dual Color LED (saved by Fritzing 0.9.3b)

parts:
  Raspberry_Pi_1 = Raspberry Pi 3 [part_number=RPI-3-V1.2]
  S1 = Dual-color led v1.0 [package=THT]

nets:
  N1: Raspberry_Pi_1.GPIO17, S1.R
  N2: Raspberry_Pi_1.GPIO18, S1.Y
  N3: Raspberry_Pi_1.GND, S1.G

custom parts:
  Dual-color led v1.0: Dual-color led v1.0 www.sunfounder.com
