# Fritzing sketch 10 RGB LED (saved by Fritzing 0.9.3b)
breadboards: 1

parts:
  T-Cobbler1 = T-Cobbler
  R1 = Resistor [tolerance=±5% resistance=220 package=THT]
  LED1 = RGB LED (com. cathode, rgb) [package="5 mm [THT]"]
  R2 = Resistor [tolerance=±5% resistance=220 package=THT]
  R3 = Resistor [tolerance=±5% resistance=220 package=THT]

nets:
  N1: T-Cobbler1.GND#4, LED1.green_anode
  N2: T-Cobbler1.GPIO17, R2.Pin_1
  N3: T-Cobbler1.GPIO27, R1.Pin_1
  N4: T-Cobbler1.GPIO18, R3.Pin_1
  N5: R1.Pin_0, LED1.blue_anode
  N6: LED1.red_anode, R2.Pin_0
  N7: LED1.common_cathode, R3.Pin_0

custom parts:
  T-Cobbler: T-Cobbler for RPi B+ and Rpi2 from SunFounder
