# Fritzing sketch 11 RGB LED Module (saved by Fritzing 0.9.3b)

parts:
  Raspberry_Pi_1 = Raspberry Pi 3 [part_number=RPI-3-V1.2]
  module1 = RGB LED

nets:
  N1: Raspberry_Pi_1.GPIO17, module1.R
  N2: Raspberry_Pi_1.GPIO27, module1.B
  N3: Raspberry_Pi_1.GPIO18, module1.G
  5V: Raspberry_Pi_1.5V, module1.VCC

custom parts:
  RGB LED: RGB LED module of SunFounder Sensor Kit
