# Fritzing sketch 12 Autoflash LED (saved by Fritzing 0.9.3b)

parts:
  Raspberry_Pi_1 = Raspberry Pi 3 [part_number=RPI-3-V1.2]
  module2 = auto-flah led v1.0

nets:
  N1: Raspberry_Pi_1.GND, module2.-
  N2: Raspberry_Pi_1.5V, module2.S

custom parts:
  auto-flah led v1.0: auto-flash led v1.0 www.sunfounder.com
