# Fritzing sketch 13 Buzzer (saved by Fritzing 0.9.3b)
breadboards: 1

parts:
  T-Cobbler1 = T-Cobbler
  J1 = Piezo Speaker
  R1 = Resistor [tolerance=±5% resistance=1k package=THT]
  Q1 = PNP-Transistor [package="TO92 [THT]"]

nets:
  N1: T-Cobbler1.3V3#0, J1.pin2
  N2: T-Cobbler1.GND#4, Q1.C
  N3: T-Cobbler1.GPIO17, R1.Pin_0
  N4: J1.pin1, Q1.E
  N5: R1.Pin_1, Q1.B

custom parts:
  T-Cobbler: T-Cobbler for RPi B+ and Rpi2 from SunFounder
