# Fritzing sketch 16 4 Channel Relay Module (saved by Fritzing 0.9.3b)

parts:
  Raspberry_Pi_1 = Raspberry Pi 3 [part_number=RPI-3-V1.2]
  Part1 = 4-Channels Relay

nets:
  N1: Raspberry_Pi_1.GPIO17, Part1.IN1
  N2: Raspberry_Pi_1.GPIO27, Part1.IN3
  N3: Raspberry_Pi_1.GPIO23, Part1.IN4
  N4: Raspberry_Pi_1.GPIO18, Part1.IN2
  GND: Raspberry_Pi_1.GND, Part1.GND
  5V: Raspberry_Pi_1.5V, Part1.VCC
