# Fritzing sketch 17 Rotary Encoder Module (saved by Fritzing 0.9.3b)

parts:
  Raspberry_Pi_1 = Raspberry Pi 3 [part_number=RPI-3-V1.2]
  module2 = Rotary Encoder

nets:
  N1: Raspberry_Pi_1.GPIO17, module2.CLK
  N2: Raspberry_Pi_1.GPIO27, module2.SW
  N3: Raspberry_Pi_1.GPIO18, module2.DT
  GND: Raspberry_Pi_1.GND, module2.GND
  5V: Raspberry_Pi_1.5V, module2.VCC

custom parts:
  Rotary Encoder: Rotary Encoder module of SunFounder Sensor Kit
