# Fritzing sketch 18 555 Timer (saved by Fritzing 0.9.3b)
breadboards: 1

parts:
  T-Cobbler1 = T-Cobbler
  U1 = 555 Timer [package="DIP8 [THT]"]
  R2 = Resistor [tolerance=±5% resistance=1k package=THT]
  R3 = Resistor [tolerance=±5% resistance=10k package=THT]
  R4 = Resistor [tolerance=±5% resistance=10k package=THT]
  C1 = Ceramic Capacitor [capacitance=100nF package="100 mil [THT, multilayer]"]
  C2 = Ceramic Capacitor [capacitance=100nF package="100 mil [THT, multilayer]"]

nets:
  N1: T-Cobbler1.GPIO17, R2.Pin_0
  N2: T-Cobbler1.5V0#20, U1.Reset, U1.Vcc_Supply_Voltage, R3.Pin_0
  N3: T-Cobbler1.GND#22, U1.Ground, C1.1, C2.0
  N4: U1.Trigger, U1.Threshold, R4.Pin_1, C2.1
  N5: U1.Output, R2.Pin_1
  N6: U1.Control_Voltage, C1.0
  N7: U1.Discharge, R3.Pin_1, R4.Pin_0

custom parts:
  T-Cobbler: T-Cobbler for RPi B+ and Rpi2 from SunFounder
