# Fritzing sketch 19 7 Segment Display (saved by Fritzing 0.9.3b)
breadboards: 1

parts:
  T-Cobbler1 = T-Cobbler
  DI2 = 7 Segment Display
  R9 = Resistor [tolerance=±5% resistance=220 package=THT]
  R10 = Resistor [tolerance=±5% resistance=220 package=THT]
  R11 = Resistor [tolerance=±5% resistance=220 package=THT]
  R12 = Resistor [tolerance=±5% resistance=220 package=THT]
  R13 = Resistor [tolerance=±5% resistance=220 package=THT]
  R14 = Resistor [tolerance=±5% resistance=220 package=THT]
  R15 = Resistor [tolerance=±5% resistance=220 package=THT]
  R16 = Resistor [tolerance=±5% resistance=220 package=THT]

nets:
  N1: T-Cobbler1.GPIO4, R9.Pin_0
  N2: T-Cobbler1.GPIO17, R10.Pin_0
  N3: T-Cobbler1.GPIO27, R11.Pin_1
  N4: T-Cobbler1.GPIO22, R12.Pin_1
  N5: T-Cobbler1.GND#22, DI2.common_cathode
  N6: T-Cobbler1.GPIO18, R14.Pin_0
  N7: T-Cobbler1.GPIO23, R13.Pin_0
  N8: T-Cobbler1.GPIO24, R15.Pin_1
  N9: T-Cobbler1.GPIO25, R16.Pin_1
  N10: DI2.Segment_E, R10.Pin_1
  N11: DI2.Segment_D, R9.Pin_1
  N12: DI2.Segment_C, R11.Pin_0
  N13: DI2.Segment_DP, R12.Pin_0
  N14: DI2.Segment_B, R16.Pin_0
  N15: DI2.Segment_A, R15.Pin_0
  N16: DI2.Segment_F, R13.Pin_1
  N17: DI2.Segment_G, R14.Pin_1

custom parts:
  T-Cobbler: T-Cobbler for RPi B+ and Rpi2 from SunFounder
