# Fritzing sketch 20 4 Digit 7 Segment Display (saved by Fritzing 0.9.3b)
breadboards: 1

parts:
  T-Cobbler1 = T-Cobbler
  R9 = Resistor [tolerance=±5% resistance=220 package=THT]
  R10 = Resistor [tolerance=±5% resistance=220 package=THT]
  R11 = Resistor [tolerance=±5% resistance=220 package=THT]
  R12 = Resistor [tolerance=±5% resistance=220 package=THT]
  R13 = Resistor [tolerance=±5% resistance=220 package=THT]
  R14 = Resistor [tolerance=±5% resistance=220 package=THT]
  R15 = Resistor [tolerance=±5% resistance=220 package=THT]
  R16 = Resistor [tolerance=±5% resistance=220 package=THT]
  LED1 = 7-SEGMENT-4DIGIT-YOUNGSUN [package=7-segment-4digit-youngsun-longpads]

nets:
  N1: T-Cobbler1.GPIO4, LED1.G
  N2: T-Cobbler1.GPIO17, LED1.COL-C
  N3: T-Cobbler1.GPIO27, LED1.DP
  N4: T-Cobbler1.GPIO22, R12.Pin_1
  N5: T-Cobbler1.GPIO5, R10.Pin_0
  N6: T-Cobbler1.GPIO18, LED1.F
  N7: T-Cobbler1.GPIO23, R13.Pin_1
  N8: T-Cobbler1.GPIO24, R16.Pin_0
  N9: T-Cobbler1.GPIO25, R9.Pin_0
  N10: T-Cobbler1.GPIO12, R11.Pin_1
  N11: T-Cobbler1.GPIO16, R14.Pin_1
  N12: T-Cobbler1.GPIO20, R15.Pin_0
  N13: R9.Pin_1, LED1.DIG2
  N14: R10.Pin_1, LED1.D
  N15: R11.Pin_0, LED1.E
  N16: R12.Pin_0, LED1.COL-A
  N17: R13.Pin_0, LED1.DIG3
  N18: R14.Pin_0, LED1.APOS-A
  N19: R15.Pin_1, LED1.A
  N20: R16.Pin_1, LED1.C

custom parts:
  T-Cobbler: T-Cobbler for RPi B+ and Rpi2 from SunFounder
  7-SEGMENT-4DIGIT-YOUNGSUN: This is a part for the 4-Digit 7-segment LEDs from Young Sun. Different from the Digikey LEDs, all 16 pins are used. The LONGPADS Variant is used for a test jig, but you may like it because there is more pad to solder to. If you are concerned about routing space, the standard works just fine though.
