# Fritzing sketch 21 7 Segment 74HC595 (saved by Fritzing 0.9.3b)
breadboards: 1

parts:
  T-Cobbler1 = T-Cobbler
  DI2 = 7 Segment Display
  R11 = Resistor [tolerance=±5% resistance=220 package=THT]
  R12 = Resistor [tolerance=±5% resistance=220 package=THT]
  R15 = Resistor [tolerance=±5% resistance=220 package=THT]
  R16 = Resistor [tolerance=±5% resistance=220 package=THT]
  U1 = 74HC595 [package="DIP16 [THT]"]
  R10 = Resistor [tolerance=±5% resistance=220 package=THT]
  R9 = Resistor [tolerance=±5% resistance=220 package=THT]
  R13 = Resistor [tolerance=±5% resistance=220 package=THT]
  R14 = Resistor [tolerance=±5% resistance=220 package=THT]

nets:
  N1: T-Cobbler1.GPIO17, U1.DS
  N2: T-Cobbler1.GPIO27, U1.SH_CP
  N3: T-Cobbler1.5V0#20, U1.MR, U1.VCC
  N4: T-Cobbler1.GND#22, DI2.common_cathode, U1.OE
  N5: T-Cobbler1.GPIO18, U1.ST_CP
  N6: DI2.Segment_E, R10.Pin_1
  N7: DI2.Segment_D, R9.Pin_1
  N8: DI2.Segment_C, R11.Pin_0
  N9: DI2.Segment_DP, R12.Pin_0
  N10: DI2.Segment_B, R16.Pin_0
  N11: DI2.Segment_A, R15.Pin_0
  N12: DI2.Segment_F, R13.Pin_1
  N13: DI2.Segment_G, R14.Pin_1
  N14: R11.Pin_1, U1.Q2
  N15: R12.Pin_1, U1.Q7
  N16: R15.Pin_1, U1.Q0
  N17: R16.Pin_1, U1.Q1
  N18: U1.Q3, R9.Pin_0
  N19: U1.Q4, R10.Pin_0
  N20: U1.Q5, R13.Pin_0
  N21: U1.Q6, R14.Pin_0

custom parts:
  T-Cobbler: T-Cobbler for RPi B+ and Rpi2 from SunFounder
