# Fritzing sketch 22 4 Digit 7 Segment 74HC595 (saved by Fritzing 0.9.3b)
breadboards: 1

parts:
  R1 = Resistor [tolerance=±5% resistance=220 package=THT]
  R2 = Resistor [tolerance=±5% resistance=220 package=THT]
  R3 = Resistor [tolerance=±5% resistance=220 package=THT]
  R4 = Resistor [tolerance=±5% resistance=220 package=THT]
  R5 = Resistor [tolerance=±5% resistance=220 package=THT]
  R6 = Resistor [tolerance=±5% resistance=220 package=THT]
  R7 = Resistor [tolerance=±5% resistance=220 package=THT]
  R8 = Resistor [tolerance=±5% resistance=220 package=THT]
  U1 = 74HC595 [package="DIP16 [THT]"]
  LED1 = 7-SEGMENT-4DIGIT-YOUNGSUN [package=7-segment-4digit-youngsun-longpads]
  R9 = Resistor [tolerance=±5% resistance=220 package=THT]
  R10 = Resistor [tolerance=±5% resistance=220 package=THT]
  R11 = Resistor [tolerance=±5% resistance=220 package=THT]
  R12 = Resistor [tolerance=±5% resistance=220 package=THT]
  U2 = 74HC595 [package="DIP16 [THT]"]
  Raspberry_Pi_1 = Raspberry Pi 3 [part_number=RPI-3-V1.2]

nets:
  N1: R1.Pin_0, LED1.DIG3
  N2: R1.Pin_1, U2.Q2
  N3: R2.Pin_0, U1.Q1
  N4: R2.Pin_1, LED1.A
  N5: R3.Pin_0, LED1.DP
  N6: R3.Pin_1, U2.Q3
  N7: R4.Pin_0, U1.Q0
  N8: R4.Pin_1, LED1.G
  N9: R5.Pin_0, LED1.DIG2
  N10: R5.Pin_1, U1.Q6
  N11: R6.Pin_0, LED1.E
  N12: R6.Pin_1, U2.Q1
  N13: R7.Pin_0, LED1.D
  N14: R7.Pin_1, U1.Q7
  N15: R8.Pin_0, LED1.COL-A
  N16: R8.Pin_1, U2.Q0
  N17: U1.Q2, R9.Pin_0
  N18: U1.Q3, R11.Pin_0
  N19: U1.Q4, R12.Pin_0
  N20: U1.Q5, R10.Pin_0
  GND: U1.GND, U1.OE, U2.GND, Raspberry_Pi_1.GND
  N21: U1.Q7', U2.DS
  VCC: U1.MR, U1.VCC, U2.MR, U2.VCC, Raspberry_Pi_1.5V
  N22: U1.SH_CP, U2.SH_CP, Raspberry_Pi_1.GPIO27
  N23: U1.ST_CP, U2.ST_CP, Raspberry_Pi_1.GPIO18
  N24: U1.DS, Raspberry_Pi_1.GPIO17
  N25: LED1.APOS-A, R10.Pin_1
  N26: LED1.F, R12.Pin_1
  N27: LED1.COL-C, R11.Pin_1
  N28: LED1.C, R9.Pin_1

custom parts:
  7-SEGMENT-4DIGIT-YOUNGSUN: This is a part for the 4-Digit 7-segment LEDs from Young Sun. Different from the Digikey LEDs, all 16 pins are used. The LONGPADS Variant is used for a test jig, but you may like it because there is more pad to solder to. If you are concerned about routing space, the standard works just fine though.
