# Fritzing sketch 23 LED 74HC595 (saved by Fritzing 0.9.3b)
breadboards: 1

parts:
  T-Cobbler1 = T-Cobbler
  U1 = 74HC595 [package="DIP16 [THT]"]
  R13 = Resistor [tolerance=±5% resistance=220 package=THT]  # not connected
  R14 = Resistor [tolerance=±5% resistance=220 package=THT]  # not connected
  R15 = Resistor [tolerance=±5% resistance=220 package=THT]  # not connected
  R16 = Resistor [tolerance=±5% resistance=220 package=THT]  # not connected
  R17 = Resistor [tolerance=±5% resistance=220 package=THT]  # not connected
  R18 = Resistor [tolerance=±5% resistance=220 package=THT]  # not connected
  R19 = Resistor [tolerance=±5% resistance=220 package=THT]  # not connected
  LED9 = LED - 5mm [color="Red (633nm)" package="5 mm [THT]"]  # not connected
  LED10 = LED - 5mm [color="Red (633nm)" package="5 mm [THT]"]  # not connected
  LED11 = LED - 5mm [color="Red (633nm)" package="5 mm [THT]"]  # not connected
  LED12 = LED - 5mm [color="Red (633nm)" package="5 mm [THT]"]  # not connected
  LED13 = LED - 5mm [color="Red (633nm)" package="5 mm [THT]"]  # not connected
  LED14 = LED - 5mm [color="Red (633nm)" package="5 mm [THT]"]  # not connected
  LED15 = LED - 5mm [color="Red (633nm)" package="5 mm [THT]"]  # not connected
  LED16 = LED - 5mm [color="Red (633nm)" package="5 mm [THT]"]  # not connected
  R20 = Resistor [tolerance=±5% resistance=220 package=THT]

nets:
  N1: T-Cobbler1.GPIO17, U1.DS
  N2: T-Cobbler1.GPIO27, U1.SH_CP
  N3: T-Cobbler1.5V0#20, U1.MR, U1.VCC
  N4: T-Cobbler1.GND#22, U1.OE
  N5: T-Cobbler1.GPIO18, U1.ST_CP
  N6: U1.GND, R20.Pin_0

custom parts:
  T-Cobbler: T-Cobbler for RPi B+ and Rpi2 from SunFounder
