# Fritzing sketch 24 Dot Matrix 74HC595 (saved by Fritzing 0.9.3b)
breadboards: 1

parts:
  Raspberry_Pi_1 = Raspberry Pi 3 [part_number=RPI-3-V1.2]
  U3 = 74HC595 [package="DIP16 [THT]"]
  U4 = 74HC595 [package="DIP16 [THT]"]
  module3 = 788BS Dot matix
  R13 = Resistor [tolerance=±5% resistance=220 package=THT]
  R14 = Resistor [tolerance=±5% resistance=220 package=THT]
  R15 = Resistor [tolerance=±5% resistance=220 package=THT]
  R16 = Resistor [tolerance=±5% resistance=220 package=THT]
  R17 = Resistor [tolerance=±5% resistance=220 package=THT]
  R18 = Resistor [tolerance=±5% resistance=220 package=THT]
  R19 = Resistor [tolerance=±5% resistance=220 package=THT]
  R20 = Resistor [tolerance=±5% resistance=220 package=THT]

nets:
  GND: Raspberry_Pi_1.GND, U3.GND, U4.GND, U4.OE, U4.DS
  N1: Raspberry_Pi_1.GPIO17, U3.SH_CP, U4.SH_CP
  N2: Raspberry_Pi_1.GPIO15, U3.ST_CP, U4.ST_CP
  VCC: Raspberry_Pi_1.5V, U3.MR, U3.VCC, U4.MR, U4.VCC
  N3: U3.Q1, module3.P3
  N4: U3.Q2, module3.P4
  N5: U3.Q3, module3.P10
  N6: U3.Q4, module3.P6
  N7: U3.Q5, module3.P11
  N8: U3.Q6, module3.P15
  N9: U3.Q7, module3.P16
  N10: U3.DS, U4.Q7'
  N11: U3.Q0, module3.P13
  N12: U4.Q1, R19.Pin_1
  N13: U4.Q2, R17.Pin_1
  N14: U4.Q3, R13.Pin_1
  N15: U4.Q4, R16.Pin_0
  N16: U4.Q5, R20.Pin_1
  N17: U4.Q6, R18.Pin_0
  N18: U4.Q7, R14.Pin_0
  N19: U4.Q0, R15.Pin_1
  N20: module3.P1, R13.Pin_0
  N21: module3.P2, R19.Pin_0
  N22: module3.P5, R15.Pin_0
  N23: module3.P7, R17.Pin_0
  N24: module3.P8, R20.Pin_0
  N25: module3.P9, R14.Pin_1
  N26: module3.P12, R16.Pin_1
  N27: module3.P14, R18.Pin_1

custom parts:
  788BS Dot matix: 788BS 8x8 dot matix from SunFounder
