# Fritzing sketch 29 LCD 1602 (saved by Fritzing 0.9.3b)
breadboards: 1

parts:
  T-Cobbler1 = T-Cobbler
  LCD1 = LCD screen
  R1 = Rotary Potentiometer (Small) [maximum_resistance=100kΩ package=THT]

nets:
  N1: T-Cobbler1.3V3#0, LCD1.VDD
  N2: T-Cobbler1.GPIO27, LCD1.RS
  N3: T-Cobbler1.GPIO22, LCD1.E
  N4: T-Cobbler1.5V0#20, LCD1.LED+, R1.leg1
  N5: T-Cobbler1.GND#22, LCD1.VSS, LCD1.R/W, LCD1.LED-, R1.leg2
  N6: T-Cobbler1.GPIO18, LCD1.DB7
  N7: T-Cobbler1.GPIO23, LCD1.DB6
  N8: T-Cobbler1.GPIO24, LCD1.DB5
  N9: T-Cobbler1.GPIO25, LCD1.DB4
  N10: LCD1.V0, R1.wiper

custom parts:
  T-Cobbler: T-Cobbler for RPi B+ and Rpi2 from SunFounder
