# Fritzing sketch 29 LCD 2004 (saved by Fritzing 0.9.3b)
breadboards: 1

parts:
  T-Cobbler1 = T-Cobbler
  R1 = Rotary Potentiometer (Small) [maximum_resistance=100kΩ package=THT]
  LCD2 = LCD 20x04

nets:
  N1: T-Cobbler1.3V3#0, LCD2.VDD
  N2: T-Cobbler1.GPIO27, LCD2.RS
  N3: T-Cobbler1.GPIO22, LCD2.E
  N4: T-Cobbler1.5V0#20, R1.leg1, LCD2.LED+
  N5: T-Cobbler1.GND#22, R1.leg2, LCD2.VSS, LCD2.R/W, LCD2.LED-
  N6: T-Cobbler1.GPIO18, LCD2.DB7
  N7: T-Cobbler1.GPIO23, LCD2.DB6
  N8: T-Cobbler1.GPIO24, LCD2.DB5
  N9: T-Cobbler1.GPIO25, LCD2.DB4
  N10: R1.wiper, LCD2.V0

custom parts:
  T-Cobbler: T-Cobbler for RPi B+ and Rpi2 from SunFounder
  LCD 20x04: LCD 2004 character display, 4x rows of 20x characters. Blue.
