# Fritzing sketch 30 I2C LCD 1602 (saved by Fritzing 0.9.3b)

parts:
  Raspberry_Pi_1 = Raspberry Pi 3 [part_number=RPI-3-V1.2]
  module1 = I2C LCD1602

nets:
  N1: Raspberry_Pi_1.GPIO2, module1.SDA
  N2: Raspberry_Pi_1.GPIO3, module1.SCL
  GND: Raspberry_Pi_1.GND, module1.GND
  5V: Raspberry_Pi_1.5V, module1.VCC

custom parts:
  I2C LCD1602: I2C LCD1602 module of SunFounder Sensor Kit
