# Fritzing sketch 36 RFID (saved by Fritzing 0.9.3b)

parts:
  Raspberry_Pi_1 = Raspberry Pi 3 [part_number=RPI-3-V1.2]
  module1 = RFID-RC522

nets:
  3V3: Raspberry_Pi_1.3v3, module1.VCC
  N1: Raspberry_Pi_1.GPIO17, module1.RST
  N2: Raspberry_Pi_1.GPIO27, module1.MOSI
  N3: Raspberry_Pi_1.GPIO22, module1.NSS
  N4: Raspberry_Pi_1.GPIO24, module1.IRQ
  N5: Raspberry_Pi_1.GPIO23, module1.SCK
  N6: Raspberry_Pi_1.GPIO18, module1.MISO
  GND: Raspberry_Pi_1.GND, module1.GND

custom parts:
  RFID-RC522: RFID-RC522 module from Sunfounder
