# Fritzing sketch 41 Analog Hall (saved by Fritzing 0.9.3b)
breadboards: 1

parts:
  T-Cobbler1 = T-Cobbler
  module1 = PCF8591
  module2 = Hall

nets:
  VCC: T-Cobbler1.3V3#0, module1.VCC, module2.VCC
  N1: T-Cobbler1.SDA1, module1.SDA
  N2: T-Cobbler1.SCL1, module1.SCL
  N3: T-Cobbler1.GPIO17, module2.DO
  GND: T-Cobbler1.GND#22, module1.GND, module2.GND
  N4: module1.AIN1, module2.AO

custom parts:
  T-Cobbler: T-Cobbler for RPi B+ and Rpi2 from SunFounder
  PCF8591: PCF8591 ADC module for SunFounder Sensor Kit
  Hall: Hall sensor module of SunFounder Sensor Kit
