# Fritzing sketch 42 Shock (saved by Fritzing 0.9.3b)

parts:
  Raspberry_Pi_1 = Raspberry Pi 3 [part_number=RPI-3-V1.2]
  S1 = Shock Switch v1.0 [package=THT]

nets:
  N1: Raspberry_Pi_1.GPIO17, S1.S
  N2: Raspberry_Pi_1.GND, S1.-
  N3: Raspberry_Pi_1.5V, S1.+

custom parts:
  Shock Switch v1.0: Shock Switch v1.0 www.sunfounder.com
