# Fritzing sketch 43 Nock (saved by Fritzing 0.9.3b)

parts:
  Raspberry_Pi_1 = Raspberry Pi 3 [part_number=RPI-3-V1.2]
  S2 = Knock Switch v1.0 [package=THT]

nets:
  N1: Raspberry_Pi_1.GPIO17, S2.S
  N2: Raspberry_Pi_1.GND, S2.-
  N3: Raspberry_Pi_1.5V, S2.+

custom parts:
  Knock Switch v1.0: Knock Switch v1.0 www.sunfounder.com
