# Fritzing sketch 44 IR T (saved by Fritzing 0.9.3b)

parts:
  Raspberry_Pi_1 = Raspberry Pi 3 [part_number=RPI-3-V1.2]
  module1 = auto-flah led v1.0

nets:
  N1: Raspberry_Pi_1.GPIO17, module1.S
  N2: Raspberry_Pi_1.GND, module1.-

custom parts:
  auto-flah led v1.0: auto-flash led v1.0 www.sunfounder.com
