# Fritzing sketch 46 Laser (saved by Fritzing 0.9.3b)

parts:
  Raspberry_Pi_1 = Raspberry Pi 3 [part_number=RPI-3-V1.2]
  S1 = Laser Transmitter v1.0 [package=THT]

nets:
  N1: Raspberry_Pi_1.GPIO17, S1.S
  N2: Raspberry_Pi_1.GND, S1.-
  N3: Raspberry_Pi_1.5V, S1.+

custom parts:
  Laser Transmitter v1.0: A laser is a device that emits light through a process of optical amplification based on the stimulated emission of electromagnetic radiation. Lasers differ from other sources of light because they emit light coherently.
