# Fritzing sketch 47 Reed Switch (saved by Fritzing 0.9.3b)

parts:
  Raspberry_Pi_1 = Raspberry Pi 3 [part_number=RPI-3-V1.2]
  module1 = Reed Switch

nets:
  N1: Raspberry_Pi_1.GPIO17, module1.SIG
  GND: Raspberry_Pi_1.GND, module1.GND
  5V: Raspberry_Pi_1.5V, module1.VCC

custom parts:
  Reed Switch: Reed Switch module of SunFounder Sensor Kit
