# Fritzing sketch 48 Analog Reed (saved by Fritzing 0.9.3b)
breadboards: 1

parts:
  T-Cobbler1 = T-Cobbler
  module1 = PCF8591
  module3 = Reed Switch V1.0

nets:
  N1: T-Cobbler1.3V3#0, module1.VCC, module3.+
  N2: T-Cobbler1.SDA1, module1.SDA
  N3: T-Cobbler1.SCL1, module1.SCL
  N4: T-Cobbler1.GPIO17, module3.D0
  N5: T-Cobbler1.GND#22, module1.GND, module3.G
  N6: module1.AIN0, module3.A0

custom parts:
  T-Cobbler: T-Cobbler for RPi B+ and Rpi2 from SunFounder
  PCF8591: PCF8591 ADC module for SunFounder Sensor Kit
  Reed Switch V1.0: A reed switch is a type of line switch component that realizes control by magnetic signals
