# Fritzing sketch 49 Photo Interrupter (saved by Fritzing 0.9.3b)

parts:
  Raspberry_Pi_1 = Raspberry Pi 3 [part_number=RPI-3-V1.2]
  module2 = Photo-interrupter

nets:
  N1: Raspberry_Pi_1.GPIO17, module2.SIG
  GND: Raspberry_Pi_1.GND, module2.GND
  5V: Raspberry_Pi_1.5V, module2.VCC

custom parts:
  Photo-interrupter: Photo-interrupter module of SunFounder Sensor Kit
