# Fritzing sketch 4N35 (saved by Fritzing 0.9.3b)
breadboards: 1

parts:
  U1 = Optocoupler [package=THT]
  LED1 = LED - 5mm [color="Red (633nm)" package="5 mm [THT]"]
  R1 = Resistor [tolerance=±5% resistance=220 package=THT]
  R2 = Resistor [tolerance=±5% resistance=1k package=THT]
  T-Cobbler1 = T-Cobbler

nets:
  N1: U1.Pin_1, R2.Pin_1
  N2: U1.Pin_2, T-Cobbler1.GPIO17
  N3: U1.Pin_4, T-Cobbler1.GND#22
  N4: U1.Pin_5, LED1.cathode
  N5: LED1.anode, R1.Pin_0
  N6: R1.Pin_1, R2.Pin_0, T-Cobbler1.5V0#20

custom parts:
  T-Cobbler: T-Cobbler for RPi B+ and Rpi2 from SunFounder
