# Fritzing sketch 51 Tilt Module (saved by Fritzing 0.9.3b)

parts:
  Raspberry_Pi_1 = Raspberry Pi 3 [part_number=RPI-3-V1.2]
  module3 = Tilt-Switch

nets:
  N1: Raspberry_Pi_1.GPIO17, module3.SIG
  GND: Raspberry_Pi_1.GND, module3.GND
  5V: Raspberry_Pi_1.5V, module3.VCC

custom parts:
  Tilt-Switch: Tilt-Switch module of SunFounder Sensor Kit
