# Fritzing sketch 52 Mercury (saved by Fritzing 0.9.3b)

parts:
  Raspberry_Pi_1 = Raspberry Pi 3 [part_number=RPI-3-V1.2]
  module4 = Mercury Switch

nets:
  N1: Raspberry_Pi_1.GPIO17, module4.SIG
  GND: Raspberry_Pi_1.GND, module4.GND
  5V: Raspberry_Pi_1.5V, module4.VCC

custom parts:
  Mercury Switch: Mercury Switch module of SunFounder Sensor Kit
