# Fritzing sketch 53 Photoresistor (saved by Fritzing 0.9.3b)
breadboards: 1

parts:
  T-Cobbler1 = T-Cobbler
  module1 = PCF8591
  R1 = PHOTOCELL [package=photocell-kit]
  R2 = Resistor [tolerance=±5% resistance=10k package=THT]

nets:
  N1: T-Cobbler1.3V3#0, module1.VCC, R1.P$1
  N2: T-Cobbler1.SDA1, module1.SDA
  N3: T-Cobbler1.SCL1, module1.SCL
  N4: T-Cobbler1.GND#22, module1.GND, R2.Pin_1
  N5: module1.AIN0, R1.P$2, R2.Pin_0

custom parts:
  T-Cobbler: T-Cobbler for RPi B+ and Rpi2 from SunFounder
  PCF8591: PCF8591 ADC module for SunFounder Sensor Kit
