# Fritzing sketch 55 Humiture (saved by Fritzing 0.9.3b)

parts:
  Raspberry_Pi_1 = Raspberry Pi 3 [part_number=RPI-3-V1.2]
  module5 = DHT11 Humiture Sensor

nets:
  N1: Raspberry_Pi_1.GPIO17, module5.SIG
  GND: Raspberry_Pi_1.GND, module5.GND
  5V: Raspberry_Pi_1.5V, module5.VCC

custom parts:
  DHT11 Humiture Sensor: DHT11 Humiture Sensor module of SunFounder Sensor Kit
