# Fritzing sketch 56 Obstacle (saved by Fritzing 0.9.3b)

parts:
  Raspberry_Pi_1 = Raspberry Pi 3 [part_number=RPI-3-V1.2]
  module6 = IR Obstacle

nets:
  N1: Raspberry_Pi_1.GPIO17, module6.SIG
  GND: Raspberry_Pi_1.GND, module6.GND
  5V: Raspberry_Pi_1.5V, module6.VCC

custom parts:
  IR Obstacle: IR Obstacle module of SunFounder Sensor Kit.
