# Fritzing sketch 57 Tracking (saved by Fritzing 0.9.3b)

parts:
  Raspberry_Pi_1 = Raspberry Pi 3 [part_number=RPI-3-V1.2]
  module7 = Tracking

nets:
  N1: Raspberry_Pi_1.GPIO17, module7.SIG
  GND: Raspberry_Pi_1.GND, module7.GND
  5V: Raspberry_Pi_1.5V, module7.VCC

custom parts:
  Tracking: Tracking module of SunFounder Sensor Kit
