# Fritzing sketch 58 Voice (saved by Fritzing 0.9.3b)
breadboards: 1

parts:
  T-Cobbler1 = T-Cobbler
  module1 = PCF8591
  module3 = Sound Sensor

nets:
  VCC: T-Cobbler1.3V3#0, module1.VCC, module3.VCC
  N1: T-Cobbler1.SDA1, module1.SDA
  N2: T-Cobbler1.SCL1, module1.SCL
  GND: T-Cobbler1.GND#22, module1.GND, module3.GND
  N3: module1.AIN0, module3.SIG

custom parts:
  T-Cobbler: T-Cobbler for RPi B+ and Rpi2 from SunFounder
  PCF8591: PCF8591 ADC module for SunFounder Sensor Kit
  Sound Sensor: Sound Sensor module of SunFounder Sensor Kit
