# Fritzing sketch 59 Metal Touch (saved by Fritzing 0.9.3b)
breadboards: 1

parts:
  T-Cobbler1 = T-Cobbler
  module1 = PCF8591
  module4 = Linear Hall Sensor(lm393)-V1.0

nets:
  N1: T-Cobbler1.3V3#0, module1.VCC, module4.+
  N2: T-Cobbler1.SDA1, module1.SDA
  N3: T-Cobbler1.SCL1, module1.SCL
  N4: T-Cobbler1.GPIO17, module4.DO
  N5: T-Cobbler1.GND#22, module1.GND, module4.G
  N6: module1.AIN0, module4.AO

custom parts:
  T-Cobbler: T-Cobbler for RPi B+ and Rpi2 from SunFounder
  PCF8591: PCF8591 ADC module for SunFounder Sensor Kit
  Linear Hall Sensor(lm393)-V1.0: Linear Hall Sensor(lm393)-V1.0 www.sunfounder.com
