# Fritzing sketch 60 Flame (saved by Fritzing 0.9.3b)
breadboards: 1

parts:
  T-Cobbler1 = T-Cobbler
  module1 = PCF8591
  module5 = Flame Sensor

nets:
  VCC: T-Cobbler1.3V3#0, module1.VCC, module5.VCC
  N1: T-Cobbler1.SDA1, module1.SDA
  N2: T-Cobbler1.SCL1, module1.SCL
  N3: T-Cobbler1.GPIO17, module5.DO
  GND: T-Cobbler1.GND#22, module1.GND, module5.GND
  N4: module1.AIN0, module5.AO

custom parts:
  T-Cobbler: T-Cobbler for RPi B+ and Rpi2 from SunFounder
  PCF8591: PCF8591 ADC module for SunFounder Sensor Kit
  Flame Sensor: Flame Sensor module of SunFounder Sensor Kit
