# Fritzing sketch 61 Gas (saved by Fritzing 0.9.3b)
breadboards: 1

parts:
  T-Cobbler1 = T-Cobbler
  module1 = PCF8591
  module6 = MQ-2 Gas Sensor

nets:
  VCC: T-Cobbler1.3V3#0, module1.VCC, module6.VCC
  N1: T-Cobbler1.SDA1, module1.SDA
  N2: T-Cobbler1.SCL1, module1.SCL
  N3: T-Cobbler1.GPIO17, module6.DO
  GND: T-Cobbler1.GND#22, module1.GND, module6.GND
  N4: module1.AIN0, module6.AO

custom parts:
  T-Cobbler: T-Cobbler for RPi B+ and Rpi2 from SunFounder
  PCF8591: PCF8591 ADC module for SunFounder Sensor Kit
  MQ-2 Gas Sensor: MQ-2 Gas Sensor module of SunFounder Sensor Kit
