# Fritzing sketch 62 Rain (saved by Fritzing 0.9.3b)
breadboards: 1

parts:
  T-Cobbler1 = T-Cobbler
  module1 = PCF8591
  module7 = LM393
  module8 = Rain Detection board

nets:
  VCC: T-Cobbler1.3V3#0, module1.VCC, module7.VCC
  N1: T-Cobbler1.SDA1, module1.SDA
  N2: T-Cobbler1.SCL1, module1.SCL
  N3: T-Cobbler1.GPIO17, module7.DO
  N4: T-Cobbler1.GND#22, module1.GND, module7.GND#8
  N5: module1.AIN0, module7.AO
  N6: module7.IN, module8.-
  N7: module7.GND#10, module8.+

custom parts:
  T-Cobbler: T-Cobbler for RPi B+ and Rpi2 from SunFounder
  PCF8591: PCF8591 ADC module for SunFounder Sensor Kit
  LM393: LM393 module of SunFounder Sensor Kit
  Rain Detection board: Rain Detection board for SunFounder Sensor Kit (along with LM393).
