# Fritzing sketch 63 Ultrasonic (saved by Fritzing 0.9.3b)

parts:
  Raspberry_Pi_1 = Raspberry Pi 3 [part_number=RPI-3-V1.2]
  module1 = Ultrasonic-HC-SRO4

nets:
  N1: Raspberry_Pi_1.GPIO17, module1.ECHO
  N2: Raspberry_Pi_1.GPIO18, module1.TRIG
  GND: Raspberry_Pi_1.GND, module1.GND
  5V: Raspberry_Pi_1.5V, module1.VCC

custom parts:
  Ultrasonic-HC-SRO4: The ultrasonic sensor uses sound to accurately detect objects and measure distances. It sends out ultrasonic waves and converts them into electronic signals
