# Fritzing sketch 64 Barometer (saved by Fritzing 0.9.3b)

parts:
  Raspberry_Pi_1 = Raspberry Pi 3 [part_number=RPI-3-V1.2]
  module1 = Barometer

nets:
  N1: Raspberry_Pi_1.GPIO2, module1.SDA
  N2: Raspberry_Pi_1.GPIO3, module1.SCL
  GND: Raspberry_Pi_1.GND, module1.GND
  5V: Raspberry_Pi_1.5V, module1.VCC

custom parts:
  Barometer: barometer module of SunFounder Sensor Kit
