# Fritzing sketch 65 RTC (saved by Fritzing 0.9.3b)

parts:
  Raspberry_Pi_1 = Raspberry Pi 3 [part_number=RPI-3-V1.2]
  module1 = DS1302 RTC

nets:
  N1: Raspberry_Pi_1.GPIO17, module1.SDA
  N2: Raspberry_Pi_1.GPIO27, module1.RST
  N3: Raspberry_Pi_1.GPIO18, module1.SCL
  GND: Raspberry_Pi_1.GND, module1.GND
  5V: Raspberry_Pi_1.5V, module1.VCC

custom parts:
  DS1302 RTC: DS1302RTC module of SunFounder Sensor Kit
