# Fritzing sketch 66 Color (saved by Fritzing 0.9.3b)

parts:
  Raspberry_Pi_1 = Raspberry Pi 3 [part_number=RPI-3-V1.2]
  module1 = Color Seneor

nets:
  N1: Raspberry_Pi_1.GPIO4, module1.OUT
  N2: Raspberry_Pi_1.GPIO17, module1.S0
  N3: Raspberry_Pi_1.GPIO27, module1.S1
  N4: Raspberry_Pi_1.GPIO22, module1.S2
  N5: Raspberry_Pi_1.GPIO18, module1.S3
  GND: Raspberry_Pi_1.GND, module1.GND
  5V: Raspberry_Pi_1.5V, module1.VCC

custom parts:
  Color Seneor: Color Sensor of SunFounder Sensor Kit for Arduino
