# Fritzing sketch 67 Liquid (saved by Fritzing 0.9.3b)
breadboards: 1

parts:
  T-Cobbler1 = T-Cobbler
  module1 = PCF8591
  module2 = Water sensor

nets:
  N1: T-Cobbler1.3V3#0, module1.VCC, module2.+
  N2: T-Cobbler1.SDA1, module1.SDA
  N3: T-Cobbler1.SCL1, module1.SCL
  N4: T-Cobbler1.GND#22, module1.GND, module2.-
  N5: module1.AIN0, module2.S

custom parts:
  T-Cobbler: T-Cobbler for RPi B+ and Rpi2 from SunFounder
  PCF8591: PCF8591 ADC module for SunFounder Sensor Kit
  Water sensor: Water sensor module of SunFounder Sensor Kit
