# Fritzing sketch 68 PIR (saved by Fritzing 0.9.3b)

parts:
  Raspberry_Pi_1 = Raspberry Pi 3 [part_number=RPI-3-V1.2]
  S1 = PIR2 [package=THT]

nets:
  N1: Raspberry_Pi_1.GPIO17, S1.OUT
  GND: Raspberry_Pi_1.GND, S1.GND
  5V: Raspberry_Pi_1.5V, S1.VCC
