# Fritzing sketch 71 LM35 (saved by Fritzing 0.9.3b)
breadboards: 1

parts:
  T-Cobbler1 = T-Cobbler
  module1 = PCF8591
  T1 = LM35 Temperature Sensor [package="TO92 [THT]"]

nets:
  N1: T-Cobbler1.3V3#0, module1.VCC, T1.+Vs
  N2: T-Cobbler1.SDA1, module1.SDA
  N3: T-Cobbler1.SCL1, module1.SCL
  GND: T-Cobbler1.GND#22, module1.GND, T1.GND
  N4: module1.AIN0, T1.Vout

custom parts:
  T-Cobbler: T-Cobbler for RPi B+ and Rpi2 from SunFounder
  PCF8591: PCF8591 ADC module for SunFounder Sensor Kit
