# Fritzing sketch DC Motor (saved by Fritzing 0.9.3b)
breadboards: 1

parts:
  IC1 = L293D [package=THT]
  M1 = DC Motor
  IC2 = Power Module [package=THT]
  T-Cobbler1 = T-Cobbler

nets:
  N1: IC1.Enable_1, T-Cobbler1.GPIO27
  N2: IC1.In_1, T-Cobbler1.GPIO18
  N3: IC1.Out_1_(_Controlled_by_Enable_1_), M1.pin_2
  N4: IC1.0V, IC2.+#10, IC2.3.3V
  N5: IC1.Out_2_(_Controlled_by_Enable_1_), M1.pin_1
  N6: IC1.In_2, T-Cobbler1.GPIO17
  N7: IC1.+Vmotor, IC2.GND#3
  N8: IC1.+V, IC2.GND#2
  N9: IC2.+#6, T-Cobbler1.GND#22

custom parts:
  Power Module: Power Module used for BreadBoard www.sunfounder.com
  T-Cobbler: T-Cobbler for RPi B+ and Rpi2 from SunFounder
