# Fritzing sketch Dot Matrix MCU (saved by Fritzing 0.9.3b)

parts:
  Part2 = Matrix LED de 8x8 basada en MAX7219
  Raspberry_Pi_1 = Raspberry Pi 3 [part_number=RPI-3-V1.2]

nets:
  VCC: Part2.VCC, Raspberry_Pi_1.5V
  GND: Part2.GND, Raspberry_Pi_1.GND
  N1: Part2.CS, Raspberry_Pi_1.GPIO17
  N2: Part2.CLK, Raspberry_Pi_1.GPIO18
  N3: Part2.DIN, Raspberry_Pi_1.GPIO27
