# Fritzing sketch Membrane Keypad (saved by Fritzing 0.9.3b)

parts:
  Raspberry_Pi_1 = Raspberry Pi 3 [part_number=RPI-3-V1.2]
  module1 = KeyPad

nets:
  N1: Raspberry_Pi_1.GPIO17, module1.X4
  N2: Raspberry_Pi_1.GPIO27, module1.X2
  N3: Raspberry_Pi_1.GPIO22, module1.Y4
  N4: Raspberry_Pi_1.GPIO5, module1.Y1
  N5: Raspberry_Pi_1.GPIO25, module1.Y2
  N6: Raspberry_Pi_1.GPIO24, module1.Y3
  N7: Raspberry_Pi_1.GPIO23, module1.X1
  N8: Raspberry_Pi_1.GPIO18, module1.X3

custom parts:
  KeyPad: Keypad module by Sunfounder
