# Fritzing sketch NRF24L01 (saved by Fritzing 0.9.3b)
breadboards: 2

parts:
  LED1 = LED - 5mm [color="Red (633nm)" package="5 mm [THT]"]
  R1 = Resistor [tolerance=±5% resistance=220 package=THT]
  S1 = Pushbutton [package="[THT]"]
  R2 = Resistor [tolerance=±5% resistance=10k package=THT]
  Part3 = NRF24L01+ Breakout Board
  Part4 = NRF24L01+ Breakout Board
  T-Cobbler1 = T-Cobbler
  T-Cobbler2 = T-Cobbler

nets:
  N1: LED1.cathode, R1.Pin_1
  N2: LED1.anode, T-Cobbler2.GPIO17
  N3: R1.Pin_0, Part4.GND
  N4: S1.Pin_1, S1.Pin_2, Part3.VCC
  N5: S1.Pin_3, S1.Pin_4, R2.Pin_0, T-Cobbler1.GPIO17
  N6: R2.Pin_1, Part3.GND
  N7: Part3.CE, T-Cobbler1.GPIO25
  N8: Part3.CS, T-Cobbler1.GPIO23
  N9: Part3.SCK, T-Cobbler1.GPIO22
  N10: Part3.MOSI, T-Cobbler1.GPIO27
  N11: Part3.MISO, T-Cobbler1.GPIO24
  N12: Part3.IRQ, T-Cobbler1.GPIO18
  N13: Part4.CE, T-Cobbler2.GPIO25
  N14: Part4.CS, T-Cobbler2.GPIO23
  N15: Part4.SCK, T-Cobbler2.GPIO22
  N16: Part4.MOSI, T-Cobbler2.GPIO27
  N17: Part4.MISO, T-Cobbler2.GPIO24
  N18: Part4.IRQ, T-Cobbler2.GPIO18

custom parts:
  T-Cobbler: T-Cobbler for RPi B+ and Rpi2 from SunFounder
