# Fritzing sketch Relay (saved by Fritzing 0.9.3b)
breadboards: 1

parts:
  Q1 = TRANSISTOR_NPN [package=to-92-ammo]
  D1 = Rectifier Diode [part_number=1N4001 package="Melf DO-213 AB [SMD]"]
  R1 = Resistor [tolerance=±5% resistance=1k package="2010 [SMD]"]
  R2 = Resistor [tolerance=±5% resistance=220 package="2010 [SMD]"]
  LED1 = LED - 5mm [color="Red (633nm)" package="5 mm [THT]"]
  OMRON1 = OMRON PCB Power Relay – G5LE [part_number="G5LE-1\n" package=THT]
  T-Cobbler1 = T-Cobbler

nets:
  N1: Q1.E, LED1.cathode, OMRON1.C, T-Cobbler1.GND#22
  N2: Q1.B, R1.Pin_0
  N3: Q1.C, D1.cathode
  N4: D1.anode, OMRON1.COIL2
  N5: R1.Pin_1, T-Cobbler1.GPIO17
  N6: R2.Pin_0, T-Cobbler1.5V0#20
  N7: R2.Pin_1, LED1.anode

custom parts:
  T-Cobbler: T-Cobbler for RPi B+ and Rpi2 from SunFounder
